# Fritzing sketch nano-bootloader-update (saved by Fritzing 0.9.4)
breadboards: 1

parts:
  Part1 = Arduino Nano (Rev3.0)
  Part2 = Arduino Nano (Rev3.0) (ICSP)

nets:
  GND: Part1.GND, Part2.GND
  N1: Part1.D10, Part2.RESET
  N2: Part1.D11/MOSI, Part2.D12/MISO
  N3: Part1.D12/MISO, Part2.D11/MOSI
  5V: Part1.5V, Part2.5V
  N4: Part1.D13/SCK, Part2.D13/SCK
